# Fritzing sketch multivibrator (saved by Fritzing 0.9.0b)
breadboards: 4

parts:
  part = Resistor [tolerance=±5% resistance=1k package=THT]
  2n3904 = TRANSISTOR_NPN [package=to-92]
  part_2 = Electrolytic Capacitor [capacitance=47µF package="0405 [SMD, electrolytic]"]
  part_3 = Resistor [tolerance=±5% resistance=56k package=THT]
  part_4 = Resistor [tolerance=±5% resistance=56k package=THT]
  part_5 = Electrolytic Capacitor [capacitance=47µF package="0405 [SMD, electrolytic]"]
  7_Segment = 7 Segment Display
  7_Segment_2 = 7 Segment Display
  2n3904_2 = TRANSISTOR_NPN [package=to-92]
  part_6 = Resistor [tolerance=±5% resistance=1k package=THT]
  part_7 = Resistor [tolerance=±5% resistance=3.3k package=THT]
  part_8 = Resistor [tolerance=±5% resistance=12k package=THT]
  part_9 = Resistor [tolerance=±5% resistance=12k package=THT]
  part_10 = Electrolytic Capacitor [capacitance=47µF package="0405 [SMD, electrolytic]"]
  part_11 = Electrolytic Capacitor [capacitance=47µF package="0405 [SMD, electrolytic]"]
  2n3904_3 = TRANSISTOR_NPN [package=to-92]
  2n3904_4 = TRANSISTOR_NPN [package=to-92]
  part_12 = Resistor [tolerance=±5% resistance=1k package=THT]
  part_13 = Resistor [tolerance=±5% resistance=1k package=THT]
  part_14 = Resistor [tolerance=±5% resistance=100k package=THT]
  part_15 = Resistor [tolerance=±5% resistance=100k package=THT]

nets (from the schematic view):
  5V: part.Pin_0, part_3.Pin_0, part_4.Pin_1, part_6.Pin_0, part_14.Pin_0, part_15.Pin_0
  N1: part.Pin_1, 2n3904.C, part_2.+
  N2: 2n3904.E, 7_Segment_2.common_anode
  N3: 2n3904.B, part_4.Pin_0, part_5.-
  N4: part_2.-, part_3.Pin_1, 2n3904_2.B
  N5: part_5.+, 2n3904_2.C, part_6.Pin_1
  N6: 7_Segment.Segment_E, 7_Segment.Segment_D, 7_Segment.Segment_C, 7_Segment_2.Segment_E, 7_Segment_2.Segment_D, 7_Segment_2.Segment_C, part_12.Pin_1
  N7: 7_Segment.common_anode, 2n3904_2.E
  N8: 7_Segment.Segment_B, 7_Segment.Segment_A, 7_Segment.Segment_F, 7_Segment_2.Segment_B, 7_Segment_2.Segment_A, 7_Segment_2.Segment_F, part_13.Pin_1
  N9: 7_Segment.Segment_G, 7_Segment_2.Segment_G, part_7.Pin_0
  GND: part_7.Pin_1, 2n3904_3.E, 2n3904_4.E
  N10: part_8.Pin_0, part_14.Pin_1
  N11: part_8.Pin_1, part_10.-, 2n3904_4.B
  N12: part_9.Pin_0, part_15.Pin_1
  N13: part_9.Pin_1, part_11.-, 2n3904_3.B
  N14: part_10.+, 2n3904_3.C, part_13.Pin_0
  N15: part_11.+, 2n3904_4.C, part_12.Pin_0
