# Fritzing sketch Dice (saved by Fritzing 0.9.0b)
perfboards: 1

parts:
  LED1 = smd LED [color="Red (633nm)" package="0805 [SMD]"]
  LED2 = smd LED [color="Red (633nm)" package="0805 [SMD]"]
  LED3 = smd LED [color="Red (633nm)" package="0805 [SMD]"]
  LED4 = smd LED [color="Red (633nm)" package="0805 [SMD]"]
  LED5 = smd LED [color="Red (633nm)" package="0805 [SMD]"]
  LED6 = smd LED [color="Red (633nm)" package="0805 [SMD]"]
  LED7 = smd LED [color="Red (633nm)" package="0805 [SMD]"]
  S1 = Pushbutton [package="[THT]"]
  U1 = attiny85 [package=dip]
  R1 = Resistor [tolerance=±5% resistance=180 package=THT]
  R2 = Resistor [tolerance=±5% resistance=180 package=THT]
  R3 = Resistor [tolerance=±5% resistance=180 package=THT]
  R4 = Resistor [tolerance=±5% resistance=330 package=THT]

nets:
  N1: LED1.cathode, LED5.anode
  N2: LED1.anode, U1.Pin_7
  N3: LED2.cathode, LED6.anode
  N4: LED2.anode, U1.Pin_6
  N5: LED3.cathode, LED7.anode
  N6: LED3.anode, U1.Pin_2
  N7: LED4.cathode, R4.Pin_0
  N8: LED4.anode, U1.Pin_3
  N9: LED5.cathode, R2.Pin_0
  N10: LED6.cathode, R1.Pin_1
  N11: LED7.cathode, R3.Pin_0
  N12: S1.Pin_1, S1.Pin_2
  N13: S1.Pin_3, S1.Pin_4, U1.Pin_5
