# Fritzing sketch OpticalTheremin (saved by Fritzing 0.9.0b)
breadboards: 1

parts:
  Part1 = Arduino Uno (Rev3) - ICSP
  J1 = Piezo Speaker
  R1 = Photocell (LDR) [package=THT]
  R2 = Resistor [tolerance=±5% resistance=1k package=THT]

nets:
  N1: Part1.A1, R1.pin_0, R2.Pin_1
  N2: Part1.D9_PWM, J1.pin1
  N3: Part1.GND, J1.pin2, R2.Pin_0
  N4: Part1.5V, R1.pin_1
