# Fritzing sketch TrinketDoorbell (saved by Fritzing 0.9.0b)
breadboards: 1

parts:
  TRINKET1 = Trinket 3V
  J1 = Piezo Speaker
  S1 = Pushbutton [package="[THT]"]

nets:
  N1: TRINKET1.no_name_yet#2, J1.pin2, S1.Pin_3, S1.Pin_4
  N2: TRINKET1.no_name_yet#4, J1.pin1
  N3: TRINKET1.no_name_yet#7, S1.Pin_1, S1.Pin_2

custom parts:
  Trinket 3V: Adafruit Trinket 3V
