# Fritzing sketch UnoDoorbell (saved by Fritzing 0.9.0b)
breadboards: 1

parts:
  J1 = Piezo Speaker
  Part1 = Arduino Uno (Rev3)
  S1 = Pushbutton [package="[THT]"]

nets:
  N1: J1.pin1, Part1.GND, S1.Pin_1, S1.Pin_2
  N2: J1.pin2, Part1.D9_PWM
  N3: Part1.D2, S1.Pin_3, S1.Pin_4
